// Digital circuit FSM_Processor.dig as structural Verilog
module FSM_Processor (
  input  clk,
  input  in_2,
  input  in_3,
  input  in_4,
  input  in_5,
  input  in_6,
  input  in_7,
  input  in_8,
  input  in_9,
  input  in_10,
  input  in_11,
  input  in_12,
  input  in_13,
  input  in_14,
  input  in_15,
  input  in_16,
  input  in_17,
  input  cmp,
  input  in_20,
  input  in_21,
  input  in_22,
  output ARSHFT
);

  wire and_1_out, and_3_out, and_4_out, and_5_out, and_6_out, and_7_out, and_8_out, and_9_out, and_10_out,
       and_11_out, and_12_out, and_13_out, and_14_out, and_15_out, and_16_out, and_17_out, and_18_out,
       and_19_out, and_20_out, and_21_out, and_22_out, and_23_out, and_24_out, and_25_out, and_26_out,
       and_27_out, and_28_out, and_29_out, and_30_out, and_31_out, lookuptable_1_out, multiplexer_1_out,
       not_1_out, not_2_out, not_3_out, not_4_out, not_5_out, not_6_out, not_7_out, not_8_out, not_9_out,
       not_10_out, not_11_out, not_12_out, not_13_out, not_14_out, not_15_out, not_16_out, not_17_out,
       not_18_out, not_19_out, not_20_out, not_21_out, not_22_out, not_23_out, not_24_out, not_25_out,
       not_26_out, not_27_out, not_28_out, not_29_out, not_30_out, not_31_out, not_32_out, not_33_out,
       not_34_out, not_35_out, not_36_out, not_37_out, not_38_out, not_39_out, not_40_out, not_41_out,
       not_42_out, not_43_out, not_44_out, not_45_out, not_47_out, not_48_out, not_49_out, not_50_out,
       not_51_out, not_52_out, not_53_out, not_54_out, not_55_out, not_56_out, not_57_out, not_58_out,
       not_59_out, not_60_out, or_1_out, or_2_out, or_3_out, or_4_out, or_5_out, or_6_out, or_7_out,
       or_8_out, or_9_out, register_1_q, register_2_q, register_3_q, register_4_q, register_5_q,
       register_6_q, register_7_q, register_8_q, register_9_q, register_10_q, register_12_q, register_13_q,
       register_14_q, register_15_q, register_16_q, register_17_q, register_18_q, register_19_q,
       register_20_q, register_21_q, register_22_q, register_23_q, register_24_q, register_25_q,
       register_26_q, register_27_q, register_28_q, register_32_q, register_33_q, register_34_q,
       register_35_q, register_36_q, register_37_q, register_38_q, register_39_q;
  wire [2:0] register_31_q;
  wire [3:0] counter_1_out;

  not not_1 (not_1_out, register_31_q[0]);
  not not_2 (not_2_out, register_31_q[0]);
  not not_3 (not_3_out, register_31_q[1]);
  not not_4 (not_4_out, register_31_q[2]);
  and and_1 (and_1_out, not_1_out, register_31_q[1]);
  and and_2 (ARSHFT, not_2_out, register_31_q[1], register_31_q[2]);
  and and_3 (and_3_out, register_31_q[0], not_3_out, not_4_out);
  not not_5 (not_5_out, clk);
  Register register_1 (.D(and_1_out), .C(not_5_out), .en(1'b1), .Q(register_1_q));
  and and_4 (and_4_out, not_6_out, register_1_q);
  not not_6 (not_6_out, clk);
  Register register_2 (.D(and_3_out), .C(not_7_out), .en(1'b1), .Q(register_2_q));
  not not_7 (not_7_out, clk);
  Register register_3 (.D(multiplexer_1_out), .C(and_4_out), .en(1'b1), .Q(register_3_q));
  Register register_4 (.D(register_3_q), .C(and_4_out), .en(1'b1), .Q(register_4_q));
  Register register_5 (.D(register_4_q), .C(and_4_out), .en(1'b1), .Q(register_5_q));
  Register register_6 (.D(register_5_q), .C(and_4_out), .en(1'b1), .Q(register_6_q));
  Register register_7 (.D(register_6_q), .C(and_4_out), .en(1'b1), .Q(register_7_q));
  Register register_8 (.D(register_7_q), .C(and_4_out), .en(1'b1), .Q(register_8_q));
  Register register_9 (.D(register_8_q), .C(and_4_out), .en(1'b1), .Q(register_9_q));
  Register register_10 (.D(register_9_q), .C(and_4_out), .en(1'b1), .Q(register_10_q));
  Register register_11 (.D(register_10_q), .C(and_4_out), .en(1'b1));  // open: Q
  or or_1 (or_1_out, register_2_q, in_21);
  and and_5 (and_5_out, clk, in_20);
  Counter #(.Bits(4)) counter_1 (.en(1'b1), .C(and_5_out), .clr(or_1_out), .out(counter_1_out));  // open: ovf
  Multiplexer #(.Selector_Bits(4)) multiplexer_1 (
    .sel(counter_1_out), .in_0(in_2), .in_1(in_4), .in_2(in_3), .in_3(in_5), .in_4(in_6), .in_5(in_8),
    .in_6(in_7), .in_7(in_9), .in_8(in_10), .in_9(in_12), .in_10(in_11), .in_11(in_13), .in_12(in_14),
    .in_13(in_16), .in_14(in_15), .in_15(in_17), .out(multiplexer_1_out));
  and and_6 (and_6_out, not_8_out, not_9_out, not_10_out, not_11_out);
  not not_8 (not_8_out, register_31_q[0]);
  not not_9 (not_9_out, register_31_q[1]);
  not not_10 (not_10_out, register_31_q[2]);
  not not_11 (not_11_out, clk);
  and and_7 (and_7_out, not_12_out, not_13_out, register_31_q[2], not_14_out);
  not not_12 (not_12_out, register_31_q[0]);
  not not_13 (not_13_out, register_31_q[1]);
  not not_14 (not_14_out, clk);
  Register register_12 (.D(multiplexer_1_out), .C(and_6_out), .en(1'b1), .Q(register_12_q));
  Register register_13 (.D(register_12_q), .C(and_6_out), .en(1'b1), .Q(register_13_q));
  Register register_14 (.D(multiplexer_1_out), .C(and_7_out), .en(1'b1), .Q(register_14_q));
  Register register_15 (.D(register_14_q), .C(and_7_out), .en(1'b1), .Q(register_15_q));
  Register register_16 (.D(register_15_q), .C(and_7_out), .en(1'b1), .Q(register_16_q));
  Register register_17 (.D(register_16_q), .C(and_7_out), .en(1'b1), .Q(register_17_q));
  Register register_18 (.D(register_17_q), .C(and_7_out), .en(1'b1), .Q(register_18_q));
  Register register_19 (.D(register_18_q), .C(and_7_out), .en(1'b1), .Q(register_19_q));
  Register register_20 (.D(register_19_q), .C(and_7_out), .en(1'b1), .Q(register_20_q));
  Register register_21 (.D(register_20_q), .C(and_7_out), .en(1'b1), .Q(register_21_q));
  Register register_22 (.D(register_21_q), .C(and_7_out), .en(1'b1), .Q(register_22_q));
  Register register_23 (.D(register_22_q), .C(and_7_out), .en(1'b1), .Q(register_23_q));
  Register register_24 (.D(register_23_q), .C(and_7_out), .en(1'b1), .Q(register_24_q));
  Register register_25 (.D(register_24_q), .C(and_7_out), .en(1'b1), .Q(register_25_q));
  Register register_26 (.D(register_25_q), .C(and_7_out), .en(1'b1), .Q(register_26_q));
  Register register_27 (.D(register_26_q), .C(and_7_out), .en(1'b1), .Q(register_27_q));
  not not_15 (not_15_out, register_31_q[0]);
  not not_16 (not_16_out, register_31_q[0]);
  not not_17 (not_17_out, register_31_q[1]);
  not not_18 (not_18_out, register_31_q[0]);
  not not_19 (not_19_out, register_31_q[1]);
  not not_20 (not_20_out, register_31_q[0]);
  not not_21 (not_21_out, register_31_q[1]);
  not not_22 (not_22_out, register_31_q[2]);
  not not_23 (not_23_out, clk);
  not not_24 (not_24_out, register_33_q);
  not not_25 (not_25_out, lookuptable_1_out);
  not not_26 (not_26_out, register_34_q);
  not not_27 (not_27_out, lookuptable_1_out);
  not not_28 (not_28_out, lookuptable_1_out);
  not not_29 (not_29_out, register_34_q);
  not not_30 (not_30_out, lookuptable_1_out);
  not not_31 (not_31_out, register_33_q);
  not not_32 (not_32_out, lookuptable_1_out);
  not not_33 (not_33_out, register_32_q);
  not not_34 (not_34_out, register_35_q);
  not not_35 (not_35_out, lookuptable_1_out);
  not not_36 (not_36_out, register_34_q);
  not not_37 (not_37_out, lookuptable_1_out);
  not not_38 (not_38_out, register_32_q);
  not not_39 (not_39_out, register_35_q);
  not not_40 (not_40_out, lookuptable_1_out);
  not not_41 (not_41_out, register_33_q);
  not not_42 (not_42_out, register_35_q);
  not not_43 (not_43_out, lookuptable_1_out);
  not not_44 (not_44_out, register_32_q);
  not not_45 (not_45_out, register_35_q);
  not not_46 (not_45_out, register_35_q);
  not not_47 (not_47_out, lookuptable_1_out);
  not not_48 (not_48_out, register_33_q);
  not not_49 (not_49_out, register_35_q);
  not not_50 (not_50_out, lookuptable_1_out);
  not not_51 (not_51_out, register_34_q);
  not not_52 (not_52_out, register_35_q);
  not not_53 (not_53_out, lookuptable_1_out);
  and and_8 (and_8_out, not_15_out, register_31_q[1]);
  and and_9 (and_9_out, not_16_out, not_17_out, register_31_q[2]);
  and and_10 (and_10_out, not_18_out, not_19_out, register_12_q, register_13_q);
  and and_11 (and_11_out, not_20_out, not_21_out, not_22_out);
  Register register_28 (.D(lookuptable_1_out), .C(not_23_out), .en(1'b1), .Q(register_28_q));
  and and_12 (and_12_out, register_32_q, not_24_out, not_25_out);
  and and_13 (and_13_out, register_32_q, not_26_out, not_27_out);
  and and_14 (and_14_out, register_33_q, register_34_q, register_35_q, not_28_out);
  and and_15 (and_15_out, register_33_q, not_29_out, not_30_out);
  and and_16 (and_16_out, not_31_out, register_34_q, register_35_q, not_32_out);
  and and_17 (and_17_out, not_33_out, register_33_q, not_34_out, not_35_out);
  and and_18 (and_18_out, not_36_out, register_35_q, not_37_out);
  and and_19 (and_19_out, not_38_out, register_34_q, not_39_out, not_40_out);
  and and_20 (and_20_out, not_41_out, register_34_q, not_42_out, not_43_out);
  and and_21 (and_21_out, not_44_out, not_45_out, not_47_out);
  and and_22 (and_22_out, not_48_out, not_49_out, not_50_out);
  and and_23 (and_23_out, not_51_out, not_52_out, not_53_out);
  or or_2 (or_2_out, and_9_out, and_10_out);
  and and_24 (and_24_out, register_28_q, clk);
  or or_3 (or_3_out, and_12_out, and_13_out, and_14_out);
  or or_4 (or_4_out, and_15_out, and_16_out, and_17_out);
  or or_5 (or_5_out, and_18_out, and_19_out, and_20_out);
  or or_6 (or_6_out, and_21_out, and_22_out, and_23_out);
  Register register_29 (.D(and_8_out), .C(and_24_out), .en(1'b1), .Q(register_31_q[0]));
  Register register_30 (.D(or_2_out), .C(and_24_out), .en(1'b1), .Q(register_31_q[1]));
  Register register_31 (.D(and_11_out), .C(and_24_out), .en(1'b1), .Q(register_31_q[2]));
  Register register_32 (.D(or_3_out), .C(clk), .en(1'b1), .Q(register_32_q));
  Register register_33 (.D(or_4_out), .C(clk), .en(1'b1), .Q(register_33_q));
  Register register_34 (.D(or_5_out), .C(clk), .en(1'b1), .Q(register_34_q));
  Register register_35 (.D(or_6_out), .C(clk), .en(1'b1), .Q(register_35_q));
  not not_54 (not_54_out, register_12_q);
  and and_25 (and_25_out, not_54_out, register_13_q, cmp);
  LookUpTable lookuptable_1 (
    .in0(register_31_q[0]), .in1(register_31_q[1]), .in2(register_31_q[2]), .in3(and_25_out),
    .in4(register_32_q), .in5(register_33_q), .in6(register_34_q), .in7(register_35_q),
    .out(lookuptable_1_out));
  and and_26 (and_26_out, register_37_q, register_38_q, register_39_q);
  and and_27 (and_27_out, register_37_q, not_55_out);
  not not_55 (not_55_out, register_38_q);
  and and_28 (and_28_out, register_37_q, not_56_out);
  not not_56 (not_56_out, register_39_q);
  and and_29 (and_29_out, not_57_out, register_38_q, register_39_q);
  not not_57 (not_57_out, register_37_q);
  and and_30 (and_30_out, not_58_out, register_39_q);
  not not_58 (not_58_out, register_38_q);
  and and_31 (and_31_out, register_38_q, not_59_out);
  not not_59 (not_59_out, register_39_q);
  not not_60 (not_60_out, register_39_q);
  or or_7 (or_7_out, register_36_q, and_26_out);
  or or_8 (or_8_out, and_27_out, and_28_out, and_29_out);
  or or_9 (or_9_out, and_30_out, and_31_out);
  Register register_36 (.D(or_7_out), .C(in_22), .en(1'b1), .Q(register_36_q));
  Register register_37 (.D(or_8_out), .C(in_22), .en(1'b1), .Q(register_37_q));
  Register register_38 (.D(or_9_out), .C(in_22), .en(1'b1), .Q(register_38_q));
  Register register_39 (.D(not_60_out), .C(in_22), .en(1'b1), .Q(register_39_q));

  // Notes on the sheet:
  //   clk: default 1
  //   contents of lookuptable_1 (hex, n*v repeats v):
  //   0,1,1,0,0,1,0,0,0,1,0,0,0,1,8*0,1,7*0,1,97*0,1,7*0,1,0,1,41*0
  //   ,1,7*0,1
endmodule
